# Fritzing sketch model (saved by Fritzing 0.9.3b)
breadboards: 1

parts:
  Composant1 = Arduino Uno (Rev3)
  R1 = Resistor [tolerance=±5% resistance=10k package=THT]
  L1 = Inductor [inductance=10mH package="400 mil [THT]"]
  D1 = Rectifier Diode [part_number=1N4001 package="300 mil [THT]"]
  R2 = Resistor [tolerance=±5% resistance=1M package=THT]
  C1 = Electrolytic Capacitor [capacitance=100pF package="100 mil [THT, electrolytic]"]
  R3 = Resistor [tolerance=±5% resistance=3.3k package=THT]
  C2 = Electrolytic Capacitor [capacitance=10nF package="100 mil [THT, electrolytic]"]

nets:
  N1: Composant1.A0, D1.cathode, R2.Pin_0, C1.-
  N2: Composant1.D9_PWM, R1.Pin_1
  N3: Composant1.GND, R2.Pin_1, C1.+, R3.Pin_1
  N4: R1.Pin_0, L1.pin_1, R3.Pin_0
  N5: L1.pin_0, D1.anode, C2.+
  Electride: C2.-
